# Fritzing sketch RBTNK-BSP-3 (saved by Fritzing 0.9.3b)
circuit board: 7.65277cm x 13.2267cm
breadboards: 2

parts:
  Arduino_Nano = Arduino Nano (Rev3.0)
  R1 = Resistor [tolerance=±5% resistance=220 package=THT]
  R2 = Resistor [tolerance=±5% resistance=220 package=THT]
  5-20V = Battery block 9V
  U1_MIDI_In = 3.5mm Audio Jack [package=audio-jack-3.5mm-smd]
  Drum_2 = 3.5mm Audio Jack [package=audio-jack]
  Drum_3 = 3.5mm Audio Jack [package=audio-jack]
  Drum_4 = 3.5mm Audio Jack [package=audio-jack]
  Drum_5 = 3.5mm Audio Jack [package=audio-jack]
  Drum_6 = 3.5mm Audio Jack [package=audio-jack]
  Drum_8 = 3.5mm Audio Jack [package=audio-jack]
  Drum_7 = 3.5mm Audio Jack [package=audio-jack]
  Drum_1 = 3.5mm Audio Jack [package=audio-jack]
  Seq2_Gate = 3.5mm Audio Jack [package=audio-jack]
  Seq2_Vel = 3.5mm Audio Jack [package=audio-jack]
  Seq2_Pitch = 3.5mm Audio Jack [package=audio-jack]
  Seq1_Vel = 3.5mm Audio Jack [package=audio-jack]
  Seq1_Gate = 3.5mm Audio Jack [package=audio-jack]
  Seq1_Pitch = 3.5mm Audio Jack [package=audio-jack]
  Clock = 3.5mm Audio Jack [package=audio-jack]
  MIDI_Out_3_Pin_Header = Header 3 [package=1x03-1mm-ra]
  R3 = Resistor [tolerance=±5% resistance=220 package=THT]
  R4 = Resistor [tolerance=±5% resistance=220 package=THT]

nets:
  N1: Arduino_Nano.D1/TX, R1.Pin_1
  N2: Arduino_Nano.D0/RX, R3.Pin_0
  N3: Arduino_Nano.GND, 5-20V.-, U1_MIDI_In.SLEEVE, Drum_2.SLEEVE, Drum_3.SLEEVE, Drum_4.SLEEVE, Drum_5.SLEEVE, Drum_6.SLEEVE, Drum_8.SLEEVE, Drum_7.SLEEVE, Drum_1.SLEEVE, Seq2_Gate.SLEEVE, Seq2_Vel.SLEEVE, Seq2_Pitch.SLEEVE, Seq1_Vel.SLEEVE, Seq1_Gate.SLEEVE, Seq1_Pitch.SLEEVE, Clock.SLEEVE, MIDI_Out_3_Pin_Header.3
  N4: Arduino_Nano.D2, Drum_8.LEFT
  N5: Arduino_Nano.D3, Drum_7.LEFT
  N6: Arduino_Nano.D4, Drum_6.LEFT
  N7: Arduino_Nano.D5, Drum_5.LEFT
  N8: Arduino_Nano.D6, Drum_4.LEFT
  N9: Arduino_Nano.D7, Drum_3.LEFT
  N10: Arduino_Nano.D8, Drum_2.LEFT
  N11: Arduino_Nano.D9, Drum_1.LEFT
  N12: Arduino_Nano.VIN, 5-20V.+
  N13: Arduino_Nano.5V, R2.Pin_1
  N14: Arduino_Nano.A6, Clock.LEFT
  N15: Arduino_Nano.A5, Seq2_Gate.LEFT
  N16: Arduino_Nano.A4, Seq2_Pitch.LEFT
  N17: Arduino_Nano.A3, Seq2_Vel.LEFT
  N18: Arduino_Nano.A2, Seq1_Gate.LEFT
  N19: Arduino_Nano.A1, Seq1_Pitch.LEFT
  N20: Arduino_Nano.A0, Seq1_Vel.LEFT
  N21: Arduino_Nano.3V3, R4.Pin_0
  N22: R1.Pin_0, U1_MIDI_In.RIGHT
  N23: R2.Pin_0, U1_MIDI_In.LEFT
  N24: MIDI_Out_3_Pin_Header.1, R3.Pin_1
  N25: MIDI_Out_3_Pin_Header.2, R4.Pin_1
